// Logisim project s-mips.circ as structural Verilog
module S_MIPS_Board (
  input  DESHABILITAR_DISPATCHER,
  output halt
);

  wire button_1_out, CLK, CS, d_ff_1_q, LCLR, LoadRAM, LoadRAMOn, LW, R_R_W, R_W, ram_dispatcher_1_finished,
       RCS, Reset_out, RST, TTY_EN;
  wire [2:0] KDB;
  wire [3:0] LMask, Mask, ram_1_read_time, ram_1_write_time, RMask;
  wire [6:0] KDB_DATA, TTY_DATA;
  wire [15:0] Addr, LAddr, RAddr;
  wire [31:0] I0, I1, I2, I3, LData, ram_1_data_out_0, ram_1_data_out_1, ram_1_data_out_2, ram_1_data_out_3,
       RI0, RI1, RI2, RI3;

  TTY #(.rows(25), .cols(80)) tty_1 (.data(TTY_DATA), .clk(CLK), .we(TTY_EN), .clr(RST));
  not not_1 (LoadRAMOn, ram_dispatcher_1_finished);
  RAM_Dispatcher ram_dispatcher_1 (
    .WriteTime(ram_1_write_time), .Clock(CLK), .Data(LData), .Address(LAddr), .Mask(LMask),
    .Finished(ram_dispatcher_1_finished), .Write(LW), .CLR(LCLR));
  Keyboard #(.buflen(64)) keyboard_1 (.clk(CLK), .re(KDB[0]), .avail(KDB[2]), .data(KDB_DATA));  // open: clr
  RAM ram_1 (
    .Address(RAddr), .Data_Out_0(ram_1_data_out_0), .Data_Out_1(ram_1_data_out_1),
    .Data_Out_2(ram_1_data_out_2), .Data_Out_3(ram_1_data_out_3), .Data_In_0(RI0), .Data_In_1(RI1),
    .Data_In_2(RI2), .Data_In_3(RI3), .Mask(RMask), .nRead_Write(R_R_W), .Chip_Select(RCS),
    .Read_Time(ram_1_read_time), .Reset(button_1_out), .Write_Time(ram_1_write_time));
  Button button_1 (.out(button_1_out));
  D_Flip_Flop d_ff_1 (.clk(CLK), .D(1'b1), .Q(d_ff_1_q), .reset(Reset_out));  // open: Qn, preset, en
  Button Reset (.out(Reset_out));
  S_MIPS s_mips_1 (
    .Kbd_Enable(KDB[0]), .Address(Addr), .Kbd_Clear(KDB[1]), .Kbd_Available(KDB[2]), .RAM_In_0(I0),
    .Kbd_ASCII_Data(KDB_DATA), .RAM_In_1(I1), .TTY_Enable(TTY_EN), .RAM_In_2(I2), .RAM_In_3(I3),
    .TTY_ASCII_Data(TTY_DATA), .Reset(RST), .RAM_Out_0(ram_1_data_out_0), .Clock(CLK),
    .RAM_Out_1(ram_1_data_out_1), .Stop(halt), .RAM_Out_2(ram_1_data_out_2), .RAM_Out_3(ram_1_data_out_3),
    .Mask(Mask), .Read_Time(ram_1_read_time), .Write_Time(ram_1_write_time), .nRead_Write(R_W),
    .Chip_Select(CS));
  D_Flip_Flop d_ff_2 (.clk(CLK), .D(d_ff_1_q), .Qn(LCLR), .reset(Reset_out));  // open: Q, preset, en
  or or_1 (RST, LCLR, LoadRAM);
  Clock clock_1 (.out(CLK));
  Multiplexer #(.width(32), .enable("false")) multiplexer_1 (.in0(I0), .in1(LData), .out(RI0), .sel(LoadRAM));
  Multiplexer #(.width(32), .enable("false")) multiplexer_2 (.in0(I1), .in1(LData), .out(RI1), .sel(LoadRAM));
  Multiplexer #(.width(32), .enable("false")) multiplexer_3 (.in0(I2), .in1(LData), .out(RI2), .sel(LoadRAM));
  Multiplexer #(.width(32), .enable("false")) multiplexer_4 (.in0(I3), .in1(LData), .out(RI3), .sel(LoadRAM));
  and and_1 (LoadRAM, ~DESHABILITAR_DISPATCHER, LoadRAMOn);  // AND_Gate
  Multiplexer #(.width(16), .enable("false")) multiplexer_5 (.in0(Addr), .in1(LAddr), .out(RAddr), .sel(LoadRAM));
  Multiplexer #(.width(4), .enable("false")) multiplexer_6 (.in0(Mask), .in1(LMask), .out(RMask), .sel(LoadRAM));
  Multiplexer #(.enable("false")) multiplexer_7 (.in0(CS), .in1(LW), .out(RCS), .sel(LoadRAM));
  Multiplexer #(.enable("false")) multiplexer_8 (.in0(R_W), .in1(LW), .out(R_R_W), .sel(LoadRAM));

  // Notes on the sheet:
  //   NO MODIFICAR
  //   Keyboard
endmodule

module RAM (
  input  [15:0] Address,
  input  [31:0] Data_In_0,
  input  [31:0] Data_In_1,
  input  [31:0] Data_In_2,
  input  [31:0] Data_In_3,
  input  [3:0] Mask,
  input  nRead_Write,
  input  Chip_Select,
  input  Reset,
  output [31:0] Data_Out_0,
  output [31:0] Data_Out_1,
  output [31:0] Data_Out_2,
  output [31:0] Data_Out_3,
  output [3:0] Read_Time,
  output [3:0] Write_Time
);

  wire and_2_out, and_3_out, and_4_out, and_5_out, and_6_out, and_7_out, and_8_out, and_9_out, Changed, CLK,
       comparator_2_eq, comparator_3_eq, comparator_4_eq, comparator_5_eq, comparator_6_eq, Count,
       demultiplexer_3_out0, Idle, Idle_q, Load, Load0, Load1, nand_1_out, or_1_out, or_2_out, or_3_out,
       or_4_out, or_5_out, or_6_out, or_7_out, or_8_out, or_9_out, or_10_out, Proc_q, Update_Mem, Zero_Time;
  wire [3:0] counter_1_q, multiplexer_1_out, subtractor_1_out;
  wire [31:0] register_1_q, register_2_q, register_3_q, register_4_q, register_5_q;

  // Probe on 4'b0011
  // Probe on 4'b0010
  Multiplexer #(.width(4), .enable("false")) multiplexer_1 (
    .in0(4'b0011), .in1(4'b0010), .out(multiplexer_1_out), .sel(nRead_Write));
  or or_1 (or_1_out, Idle, Update_Mem);
  or or_2 (or_2_out, ~Chip_Select, Reset);  // OR_Gate
  Subtractor #(.width(4)) subtractor_1 (.a(multiplexer_1_out), .b(4'b0010), .out(subtractor_1_out));  // open: bin, bout
  D_Flip_Flop u_Idle (.clk(CLK), .D(or_1_out), .Q(Idle_q), .preset(or_2_out));  // open: Qn, en, reset
  Demultiplexer #(.enable("false")) demultiplexer_1 (.out0(Idle), .out1(Load0), .in(Idle_q), .sel(Changed));
  // Probe on counter_1_q
  Counter #(.width(4), .max('hf)) counter_1 (
    .load(Load), .D(subtractor_1_out), .count(Count), .Q(counter_1_q), .clk(CLK), .clr(or_3_out));  // open: carry
  or or_3 (or_3_out, ~Chip_Select, Reset);  // OR_Gate
  Comparator #(.width(4), .mode("unsigned")) comparator_1 (
    .a(4'b0000), .b(counter_1_q), .eq(Zero_Time));  // open: gt, lt
  or or_4 (or_4_out, Count, Load0, Load1);
  Register #(.width(32)) register_1 (.D(Data_In_0), .en(Chip_Select), .Q(register_1_q), .clk(CLK), .clr(or_5_out));
  or or_5 (or_5_out, ~Chip_Select, Reset);  // OR_Gate
  Register #(.width(32)) register_2 (.D(Data_In_1), .en(Chip_Select), .Q(register_2_q), .clk(CLK), .clr(or_6_out));
  or or_6 (or_6_out, ~Chip_Select, Reset);  // OR_Gate
  Register #(.width(32)) register_3 (.D(Data_In_2), .en(Chip_Select), .Q(register_3_q), .clk(CLK), .clr(or_7_out));
  or or_7 (or_7_out, ~Chip_Select, Reset);  // OR_Gate
  Register #(.width(32)) register_4 (.D(Data_In_3), .en(Chip_Select), .Q(register_4_q), .clk(CLK), .clr(or_8_out));
  or or_8 (or_8_out, ~Chip_Select, Reset);  // OR_Gate
  Register #(.width(32)) register_5 (
    .D({{11{1'b1}}, nRead_Write, Mask, Address}), .en(Chip_Select), .Q(register_5_q), .clk(CLK),
    .clr(or_9_out));
  or or_9 (or_9_out, ~Chip_Select, Reset);  // OR_Gate
  D_Flip_Flop Proc (.clk(CLK), .D(or_4_out), .Q(Proc_q), .reset(or_10_out));  // open: Qn, preset, en
  or or_10 (or_10_out, ~Chip_Select, Reset);  // OR_Gate
  Demultiplexer #(.enable("false")) demultiplexer_2 (
    .out0(Count), .out1(Update_Mem), .in(demultiplexer_3_out0), .sel(Zero_Time));
  Demultiplexer #(.enable("false")) demultiplexer_3 (
    .out0(demultiplexer_3_out0), .out1(Load1), .in(Proc_q), .sel(Changed));
  Clock clock_1 (.out(CLK));
  Comparator #(.width(32)) comparator_2 (.a(register_1_q), .b(Data_In_0), .eq(comparator_2_eq));  // open: gt, lt
  Comparator #(.width(32)) comparator_3 (.a(register_2_q), .b(Data_In_1), .eq(comparator_3_eq));  // open: gt, lt
  Comparator #(.width(32)) comparator_4 (.a(register_3_q), .b(Data_In_2), .eq(comparator_4_eq));  // open: gt, lt
  Comparator #(.width(32)) comparator_5 (.a(register_4_q), .b(Data_In_3), .eq(comparator_5_eq));  // open: gt, lt
  Comparator #(.width(32)) comparator_6 (
    .a(register_5_q), .b({{11{1'b1}}, nRead_Write, Mask, Address}), .eq(comparator_6_eq));  // open: gt, lt
  nand nand_1 (nand_1_out, comparator_6_eq, comparator_2_eq, comparator_3_eq, comparator_4_eq, comparator_5_eq);
  and and_1 (Changed, nand_1_out, Chip_Select);
  or or_11 (Load, Count, Load1, Load0);
  and and_2 (and_2_out, Mask[0], Update_Mem, nRead_Write);
  and and_3 (and_3_out, Mask[1], Update_Mem, nRead_Write);
  and and_4 (and_4_out, Mask[2], Update_Mem, nRead_Write);
  and and_5 (and_5_out, Mask[3], Update_Mem, nRead_Write);
  RAM_part #(.addrWidth(16), .dataWidth(32), .bus("separate")) ram_1 (
    .addr(Address), .din(Data_In_0), .data(Data_Out_0), .str(and_2_out), .sel(Chip_Select), .clk(CLK),
    .ld(and_6_out), .clr(Reset));
  and and_6 (and_6_out, ~nRead_Write, Idle);  // AND_Gate
  RAM_part #(.addrWidth(16), .dataWidth(32), .bus("separate")) ram_2 (
    .addr(Address), .din(Data_In_1), .data(Data_Out_1), .str(and_3_out), .sel(Chip_Select), .clk(CLK),
    .ld(and_7_out), .clr(Reset));
  and and_7 (and_7_out, ~nRead_Write, Idle);  // AND_Gate
  RAM_part #(.addrWidth(16), .dataWidth(32), .bus("separate")) ram_3 (
    .addr(Address), .din(Data_In_2), .data(Data_Out_2), .str(and_4_out), .sel(Chip_Select), .clk(CLK),
    .ld(and_8_out), .clr(Reset));
  and and_8 (and_8_out, ~nRead_Write, Idle);  // AND_Gate
  RAM_part #(.addrWidth(16), .dataWidth(32), .bus("separate")) ram_4 (
    .addr(Address), .din(Data_In_3), .data(Data_Out_3), .str(and_5_out), .sel(Chip_Select), .clk(CLK),
    .ld(and_9_out), .clr(Reset));
  and and_9 (and_9_out, ~nRead_Write, Idle);  // AND_Gate

  assign Read_Time = 4'b0011;
  assign Write_Time = 4'b0010;

  // Other names for the same wires on the sheet: M0 = Mask[0]; M1 = Mask[1]; M2 = Mask[2]; M3 = Mask[3];
  //   RW = nRead_Write; CLR = Reset; CS = Chip_Select; Load2 = Count

  // Notes on the sheet:
  //   NO MODIFICAR
  //   excepto quizás los valores RT y WT
  //   BANK0
  //   BANK1
  //   BANK2
  //   BANK3
endmodule

module S_MIPS (
  input  Kbd_Available,
  input  [6:0] Kbd_ASCII_Data,
  input  [31:0] RAM_Out_0,
  input  [31:0] RAM_Out_1,
  input  Reset,
  input  [31:0] RAM_Out_2,
  input  Clock,
  input  [31:0] RAM_Out_3,
  input  [3:0] Read_Time,
  input  [3:0] Write_Time,
  output Kbd_Enable,
  output [15:0] Address,
  output Kbd_Clear,
  output TTY_Enable,
  output [6:0] TTY_ASCII_Data,
  output Stop,
  output [31:0] RAM_In_0,
  output [31:0] RAM_In_1,
  output [31:0] RAM_In_2,
  output [31:0] RAM_In_3,
  output [3:0] Mask,
  output nRead_Write,
  output Chip_Select
);

  Branch_Control branch_control_1 ();  // open: in_6, in_9, in_1, in_4, in_7, Program_Counter, RA, jump, jump_jr, branch, in_10, in_11, in_13, in_14, in_12, in_15
  Data_Path data_path_1 ();  // open: Instruction, in_3, Rd, Rt, Rs, in_13, in_6, func_code, op_code, offset, kbd, rst, clk, in_15, stackOp
  ID id_1 ();  // open: Output, Output_3, Output_4, Output_8, Output_5, Output_7, Output_2, Output_6, PC, RST, CLK, nRt_Rd, push_pop, isJ, isJr, branch, branchT

  // Other names for the same wires on the sheet: CLK = Clock; CLR = Reset; CS = Chip_Select;
  //   KBD_AVAIL = Kbd_Available; KBD_CLR = Kbd_Clear; KBD_DATA[6:0] = Kbd_ASCII_Data; RAM_A[15:0] = Address;
  //   RAM_INPUT_0[31:0] = RAM_In_0; RAM_INPUT_1[31:0] = RAM_In_1; RAM_INPUT_2[31:0] = RAM_In_2;
  //   RAM_INPUT_3[31:0] = RAM_In_3; RAM_MASK[3:0] = Mask; RAM_OUTPUT_0[31:0] = RAM_Out_0;
  //   RAM_OUTPUT_1[31:0] = RAM_Out_1; RAM_OUTPUT_2[31:0] = RAM_Out_2; RAM_OUTPUT_3[31:0] = RAM_Out_3;
  //   RW = nRead_Write; TTY_DATA[6:0] = TTY_ASCII_Data

  // Notes on the sheet:
  //   RAM ADDRESS
  //   DATA FROM RAM
  //   DATA TO RAM
  //   DATA WRITE MASK
  //   RAM TIMING
  //   RAM CONTROL
  //   KEYBOARD
  //   TTY
  //   SEQUENCING
endmodule

module RAM_Dispatcher (
  input  [3:0] WriteTime,
  input  Clock,
  input  CLR,
  output [31:0] Data,
  output [15:0] Address,
  output [3:0] Mask,
  output Finished,
  output Write
);

  wire demultiplexer_2_out1, demultiplexer_3_out1, End, IDLE_q, IncAddr, Load, or_1_out, or_2_out, While_q,
       WriteEnd;
  wire [3:0] counter_1_q;
  wire [31:0] CurrentAddress_q;

  Counter #(.width(32), .max('hffffffff)) CurrentAddress (
    .count(IncAddr), .Q({CurrentAddress_q[31:18], Address, CurrentAddress_q[1:0]}), .clk(Clock), .clr(CLR));  // open: load, D, carry
  or or_1 (or_1_out, IncAddr, demultiplexer_3_out1, Finished);
  D_Flip_Flop IDLE (.clk(Clock), .D(or_1_out), .Q(IDLE_q), .preset(CLR));  // open: Qn, en, reset
  Demultiplexer #(.enable("false")) demultiplexer_1 (.out0(Load), .out1(Finished), .in(IDLE_q), .sel(End));
  D_Flip_Flop While (.clk(Clock), .D(or_2_out), .Q(While_q), .reset(CLR));  // open: Qn, preset, en
  or or_2 (or_2_out, Write, Load);
  RAM_part #(.addrWidth(18), .dataWidth(32)) ram_1 (
    .addr({Address, CurrentAddress_q[1:0]}), .data(Data), .clk(Clock));  // open: sel, ld, clr
  Demultiplexer #(.enable("false")) demultiplexer_2 (
    .out0(Write), .out1(demultiplexer_2_out1), .in(While_q), .sel(WriteEnd));
  Decoder #(.select(2)) decoder_1 (
    .out0(Mask[0]), .out1(Mask[1]), .out2(Mask[2]), .out3(Mask[3]), .sel(CurrentAddress_q[1:0]));  // open: en
  Demultiplexer #(.enable("false")) demultiplexer_3 (
    .out0(IncAddr), .out1(demultiplexer_3_out1), .in(demultiplexer_2_out1), .sel(End));
  Counter #(.width(4), .max('hf)) counter_1 (
    .load(Load), .D(WriteTime), .count(Write), .Q(counter_1_q), .clk(Clock));  // open: carry, clr
  Comparator #(.width(32)) comparator_1 (.a(Data), .b({32{1'b1}}), .eq(End));  // open: gt, lt
  Comparator #(.width(4)) comparator_2 (.a(4'b0000), .b(counter_1_q), .eq(WriteEnd));  // open: gt, lt

  // Other names for the same wires on the sheet: CLK = Clock; Count = Write; WT[3:0] = WriteTime
endmodule

module Register_File (
  input  MD,
  input  Reset,
  input  [4:0] A,
  input  [4:0] B,
  input  [31:0] DI,
  input  RW,
  input  Clk,
  input  [4:0] DA,
  input  [31:0] HI_value,
  input  [31:0] LO_value,
  output [31:0] RA,
  output [31:0] RB,
  output [31:0] Stack_Pointer,
  output [31:0] HI_value_2,
  output [31:0] LO_value_2
);

  wire R1, R2, R3, R4, R5, R6, R7, R8, R9, R10, R11, R12, R13, R14, R15, R16, R17, R18, R19, R20, R21, R22,
       R23, R24, R25, R26, R27, R28, R29, R30, R31;
  wire [31:0] O19, OR0, OR1, OR2, OR3, OR4, OR5, OR6, OR7, OR8, OR9, OR10, OR11, OR12, OR13, OR14, OR15,
       OR16, OR17, OR18, OR19, OR20, OR21, OR22, OR23, OR24, OR25, OR26, OR27, OR28, OR29, OR30;

  Decoder #(.select(5), .disabled(0)) decoder_1 (
    .out1(R1), .out2(R2), .out3(R3), .out4(R4), .out5(R5), .out6(R6), .out7(R7), .out8(R8), .out9(R9),
    .out10(R10), .out11(R11), .out12(R12), .out13(R13), .out14(R14), .out15(R15), .out16(R16), .out17(R17),
    .out18(R18), .out19(R19), .out20(R20), .out21(R21), .out22(R22), .out23(R23), .out24(R24), .out25(R25),
    .out26(R26), .out27(R27), .out28(R28), .out29(R29), .out30(R30), .out31(R31), .sel(DA), .en(RW));  // open: out0
  Multiplexer #(.select(5), .width(32), .disabled(0), .enable("false")) multiplexer_1 (
    .in1(OR1), .in2(OR2), .in3(OR3), .in4(OR4), .in5(OR5), .in6(OR6), .in7(OR7), .in8(OR8), .in9(OR9),
    .in10(OR10), .in11(OR11), .in12(OR12), .in13(OR13), .in14(OR14), .in15(OR15), .in16(OR16), .in17(OR17),
    .in18(OR18), .in19(O19), .in20(OR20), .in21(OR21), .in22(OR22), .in23(OR23), .in24(OR24), .in25(OR25),
    .in26(OR26), .in27(OR27), .in28(OR28), .in29(OR29), .in30(OR30), .in31(Stack_Pointer), .out(RA), .sel(A));  // open: in0
  Multiplexer #(.select(5), .width(32), .disabled(0), .enable("false")) multiplexer_2 (
    .in1(OR1), .in2(OR2), .in3(OR3), .in4(OR4), .in5(OR5), .in6(OR6), .in7(OR7), .in8(OR8), .in9(OR9),
    .in10(OR10), .in11(OR11), .in12(OR12), .in13(OR13), .in14(OR14), .in15(OR15), .in16(OR16), .in17(OR17),
    .in18(OR18), .in19(O19), .in20(OR20), .in21(OR21), .in22(OR22), .in23(OR23), .in24(OR24), .in25(OR25),
    .in26(OR26), .in27(OR27), .in28(OR28), .in29(OR29), .in30(OR30), .in31(Stack_Pointer), .out(RB), .sel(B));  // open: in0
  Register #(.width(32)) register_1 (.D({32{1'b0}}), .Q(OR0), .clk(Clk), .clr(Reset));  // open: en
  Register #(.width(32)) register_2 (.D(DI), .en(R8), .Q(OR8), .clk(Clk), .clr(Reset));
  Register #(.width(32)) register_3 (.D(DI), .en(R16), .Q(OR16), .clk(Clk), .clr(Reset));
  Register #(.width(32)) register_4 (.D(DI), .en(R24), .Q(OR24), .clk(Clk), .clr(Reset));
  Register #(.width(32)) register_5 (.D(DI), .en(R1), .Q(OR1), .clk(Clk), .clr(Reset));
  Register #(.width(32)) register_6 (.D(DI), .en(R9), .Q(OR9), .clk(Clk), .clr(Reset));
  Register #(.width(32)) register_7 (.D(DI), .en(R17), .Q(OR17), .clk(Clk), .clr(Reset));
  Register #(.width(32)) register_8 (.D(DI), .en(R25), .Q(OR25), .clk(Clk), .clr(Reset));
  Register #(.width(32)) HI (.D(HI_value), .en(MD), .Q(HI_value_2), .clk(Clk), .clr(Reset));
  Register #(.width(32)) register_9 (.D(DI), .en(R2), .Q(OR2), .clk(Clk), .clr(Reset));
  Register #(.width(32)) register_10 (.D(DI), .en(R10), .Q(OR10), .clk(Clk), .clr(Reset));
  Register #(.width(32)) register_11 (.D(DI), .en(R18), .Q(OR18), .clk(Clk), .clr(Reset));
  Register #(.width(32)) register_12 (.D(DI), .en(R26), .Q(OR26), .clk(Clk), .clr(Reset));
  Register #(.width(32)) register_13 (.D(DI), .en(R3), .Q(OR3), .clk(Clk), .clr(Reset));
  Register #(.width(32)) register_14 (.D(DI), .en(R11), .Q(OR11), .clk(Clk), .clr(Reset));
  Register #(.width(32)) register_15 (.D(DI), .en(R19), .Q(OR19), .clk(Clk), .clr(Reset));
  Register #(.width(32)) register_16 (.D(DI), .en(R27), .Q(OR27), .clk(Clk), .clr(Reset));
  Register #(.width(32)) register_17 (.D(DI), .en(R4), .Q(OR4), .clk(Clk), .clr(Reset));
  Register #(.width(32)) register_18 (.D(DI), .en(R12), .Q(OR12), .clk(Clk), .clr(Reset));
  Register #(.width(32)) register_19 (.D(DI), .en(R20), .Q(OR20), .clk(Clk), .clr(Reset));
  Register #(.width(32)) register_20 (.D(DI), .en(R28), .Q(OR28), .clk(Clk), .clr(Reset));
  Register #(.width(32)) LO (.D(LO_value), .en(MD), .Q(LO_value_2), .clk(Clk), .clr(Reset));
  Register #(.width(32)) register_21 (.D(DI), .en(R5), .Q(OR5), .clk(Clk), .clr(Reset));
  Register #(.width(32)) register_22 (.D(DI), .en(R13), .Q(OR13), .clk(Clk), .clr(Reset));
  Register #(.width(32)) register_23 (.D(DI), .en(R21), .Q(OR21), .clk(Clk), .clr(Reset));
  Register #(.width(32)) register_24 (.D(DI), .en(R29), .Q(OR29), .clk(Clk), .clr(Reset));
  Register #(.width(32)) register_25 (.D(DI), .en(R6), .Q(OR6), .clk(Clk), .clr(Reset));
  Register #(.width(32)) register_26 (.D(DI), .en(R14), .Q(OR14), .clk(Clk), .clr(Reset));
  Register #(.width(32)) register_27 (.D(DI), .en(R22), .Q(OR22), .clk(Clk), .clr(Reset));
  Register #(.width(32)) register_28 (.D(DI), .en(R30), .Q(OR30), .clk(Clk), .clr(Reset));
  Register #(.width(32)) register_29 (.D(DI), .en(R7), .Q(OR7), .clk(Clk), .clr(Reset));
  Register #(.width(32)) register_30 (.D(DI), .en(R15), .Q(OR15), .clk(Clk), .clr(Reset));
  Register #(.width(32)) register_31 (.D(DI), .en(R23), .Q(OR23), .clk(Clk), .clr(Reset));
  Register #(.width(32)) register_32 (.D(DI), .en(R31), .Q(Stack_Pointer), .clk(Clk), .clr(Reset));

  // Other names for the same wires on the sheet: OR31[31:0] = Stack_Pointer
endmodule

module ALU (
  input  [31:0] A,
  input  [31:0] B,
  input  [3:0] in_3,
  output ZF,
  output [31:0] RESULT,
  output NF,
  output [31:0] HIGH
);

  wire comparator_1_lt, comparator_2_lt;
  wire [31:0] AND, DIV, DIV_HIGH, DIVU, DIVU_HIGH, MUL, MUL_HIGH, MULU, MULU_HIGH, NOR, OR, SLT, SLTU, SUB,
       SUM, undriven, undriven_2, undriven_3, undriven_4, undriven_5, undriven_6, undriven_7, undriven_8,
       undriven_9, undriven_10, undriven_11, undriven_12, undriven_13, XOR;

  Adder #(.width(32)) adder_1 (.a(A), .b(B), .out(SUM));  // open: cin, cout
  Subtractor #(.width(32)) subtractor_1 (.a(A), .b(B), .out(SUB));  // open: bin, bout
  Comparator #(.width(32)) comparator_1 (.a(A), .b(B), .lt(comparator_1_lt));  // open: gt, eq
  Comparator #(.width(32), .mode("unsigned")) comparator_2 (.a(A), .b(B), .lt(comparator_2_lt));  // open: gt, eq
  assign SLT = {{31{1'b0}}, comparator_1_lt};  // Bit_Extender bit_extender_1
  assign SLTU = {{31{1'b0}}, comparator_2_lt};  // Bit_Extender bit_extender_2
  assign AND = A & B;  // AND_Gate and_1, 32 bits wide
  assign NOR = ~(A | B);  // NOR_Gate nor_1, 32 bits wide
  assign XOR = A ^ B;  // XOR_Gate xor_1, 32 bits wide
  assign OR = A | B;  // OR_Gate or_1, 32 bits wide
  MULU mulu_1 (.A(A), .B(B), .L(MULU), .H(MULU_HIGH));
  DIVU divu_1 (.A(A), .B(B), .L(DIVU), .H(DIVU_HIGH));
  Multiplier #(.width(32)) multiplier_1 (.a(A), .b(B), .out(MUL), .cout(MUL_HIGH));  // open: cin
  Divider #(.width(32)) divider_1 (.a(A), .b(B), .out(DIV), .rem(DIV_HIGH));  // open: upper
  Multiplexer #(.select(4), .width(32), .disabled(0), .enable("false")) multiplexer_1 (
    .in0(undriven_10), .in1(undriven_9), .in2(undriven_8), .in3(undriven_7), .in4(undriven_5),
    .in5(undriven_4), .in6(undriven_3), .in7(undriven), .in8(undriven_2), .in9(undriven_11),
    .in10(undriven_12), .in11(undriven_13), .in12(undriven_6), .out(RESULT), .sel(in_3));  // open: in13, in14, in15
  Comparator #(.width(32)) comparator_3 (.a(RESULT), .b({32{1'b0}}), .eq(ZF), .lt(NF));  // open: gt

  // Other names for the same wires on the sheet: Selector[3:0] = in_3

  // Notes on the sheet:
  //   INPUT
  //   OPS
  //   OUTPUT
endmodule

module MULU (
  input  [31:0] A,
  input  [31:0] B,
  output [31:0] L,
  output [31:0] H
);

  wire [31:0] abs_1_a_2, abs_2_a_2;

  ABS abs_1 (.A(A), .A_2(abs_1_a_2));
  ABS abs_2 (.A(B), .A_2(abs_2_a_2));
  Multiplier #(.width(32)) multiplier_1 (.a(abs_1_a_2), .b(abs_2_a_2), .out(L), .cout(H));  // open: cin

  // Other names for the same wires on the sheet: MULU_HIGH[31:0] = H; MULU_LOW[31:0] = L

  // Notes on the sheet:
  //   INPUT
  //   OUTPUT
endmodule

module DIVU (
  input  [31:0] A,
  input  [31:0] B,
  output [31:0] L,
  output [31:0] H
);

  wire [31:0] abs_1_a_2, abs_2_a_2;

  ABS abs_1 (.A(A), .A_2(abs_1_a_2));
  ABS abs_2 (.A(B), .A_2(abs_2_a_2));
  Multiplier #(.width(32)) multiplier_1 (.a(abs_1_a_2), .b(abs_2_a_2), .out(L), .cout(H));  // open: cin

  // Other names for the same wires on the sheet: DIVU_HIGH[31:0] = H; DIVU_LOW[31:0] = L

  // Notes on the sheet:
  //   INPUT
  //   OUTPUT
endmodule

module ABS (
  input  [31:0] A,
  output [31:0] A_2
);

  wire [31:0] and_1_out, and_2_out, EXT_Sign_A, negator_1_out, not_1_out;

  assign EXT_Sign_A = {{31{A[31]}}, A[31]};  // Bit_Extender bit_extender_1
  // Probe on A
  Negator #(.width(32)) negator_1 (.in(A), .out(negator_1_out));
  // Probe on A_2
  assign and_1_out = EXT_Sign_A & negator_1_out;  // AND_Gate and_1, 32 bits wide
  assign not_1_out = ~EXT_Sign_A;  // NOT_Gate not_1, 32 bits wide
  assign and_2_out = not_1_out & A;  // AND_Gate and_2, 32 bits wide
  assign A_2 = and_1_out | and_2_out;  // OR_Gate or_1, 32 bits wide

  // Other names for the same wires on the sheet: Sign_A = A[31]; A_t[31:0] = A_2

  // Notes on the sheet:
  //   INPUT
  //   OUTPUT
endmodule

module Branch_Control (
  input  [15:0] in_1,
  input  [31:0] RA,
  input  jump,
  input  [1:0] in_4,
  input  jump_jr,
  input  in_6,
  input  [31:0] in_7,
  input  branch,
  input  in_9,
  input  [2:0] in_10,
  input  in_11,
  input  in_12,
  input  in_13,
  input  in_14,
  input  in_15,
  output [31:0] Program_Counter
);

  wire branch_taken, or_1_out;
  wire [27:0] adder_2_out;
  wire [30:0] j_adress;
  wire [31:0] bit_extender_1_out, branch_adress, multiplier_1_out, next_pc, normal_adress, PC_4;

  or or_1 (or_1_out, in_11, in_13);
  Multiplexer #(.select(3)) multiplexer_1 (
    .in0(in_12), .in1(or_1_out), .in2(in_14), .in3(in_11), .out(branch_taken), .sel(in_10));  // open: in4, in5, in6, in7, en
  or or_2 (in_4[0], jump_jr, jump);
  or or_3 (in_4[1], jump_jr, branch_taken);
  Register #(.width(32), .trigger("falling")) u_PROGRAM_COUNTER (
    .D(in_7), .Q(Program_Counter), .clk(in_6), .clr(in_9));  // open: en
  Adder #(.width(32)) adder_1 (.a(in_7), .b(32'h4), .out(normal_adress));  // open: cin, cout
  Adder #(.width(32)) adder_2 (.a(in_7), .b(32'h4), .out({j_adress[3:0], adder_2_out}));  // open: cin, cout
  Multiplexer #(.select(2), .width(32), .enable("false")) multiplexer_2 (
    .in0(normal_adress), .in1({1'b0, j_adress[30:23], 1'b0, j_adress[21:0]}), .in2(branch_adress), .in3(RA),
    .out(next_pc), .sel(in_4));
  assign bit_extender_1_out = {{16{in_1[15]}}, in_1};  // Bit_Extender bit_extender_1
  Multiplier #(.width(32)) multiplier_1 (.a(bit_extender_1_out), .b(32'h4), .out(multiplier_1_out));  // open: cin, cout
  Adder #(.width(32)) adder_3 (.a(PC_4), .b(multiplier_1_out), .out(branch_adress));  // open: cin, cout

  assign in_15 = in_12;

  // Other names for the same wires on the sheet: branchType[2:0] = in_10; clk = in_6; equal = in_12; nequal = in_12;
  //   ez_flag = in_13; gtz_flag = in_14; j = jump; PC_4_high[3:0] = j_adress[3:0];
  //   jump_t[25:0] = {j_adress[30:23], j_adress[21:4]}; jr = jump_jr; jr_adress[31:0] = RA; ltz_flag = in_11;
  //   offset[15:0] = in_1; pc[31:0] = in_7; prc_source[1:0] = in_4; rst = in_9

  // Notes on the sheet:
  //   Input
  //   NEXT INSTRUCTION SELECTION
  //   NEXT INSTRUCTION CALCULATOR
endmodule

module ID (
  input  [31:0] PC,
  input  RST,
  input  CLK,
  output [5:0] Output,
  output [31:0] Output_2,
  output push_pop,
  output [4:0] Output_3,
  output isJ,
  output [4:0] Output_4,
  output [25:0] Output_5,
  output isJr,
  output [4:0] Output_6,
  output branch,
  output [15:0] Output_7,
  output [5:0] Output_8,
  output [2:0] branchT,
  output nRt_Rd
);

  wire _111000, and_6_out, and_13_out, and_14_out, I, is_beq, is_blez, is_bltz, is_bne, is_lw, is_pop,
       is_push, is_sw, nop, nor_1_out, nor_2_out, nor_3_out, nor_4_out, nor_5_out, nor_6_out, nor_7_out,
       nor_8_out, nor_9_out, not_1_out, not_2_out, or_3_out;

  Register #(.width(32)) INSTRUCTION_MEMORY (
    .D(PC), .Q({Output_2[31:17], Output_2[27], Output_2[15:6], Output}), .clk(CLK), .clr(RST));  // open: en
  not not_1 (not_1_out, Output_2[27]);
  nor nor_1 (nor_1_out, Output_2[27], Output_2[28]);
  nor nor_2 (nor_2_out, Output_2[26], Output_2[27]);
  and and_1 (is_beq, nor_2_out, Output_2[28], nor_3_out);
  and and_2 (is_bne, Output_2[26], Output_2[28], not_1_out, nor_3_out);
  not not_2 (not_2_out, Output_2[26]);
  and and_3 (is_blez, not_2_out, Output_2[27], Output_2[28], nor_3_out);
  and and_4 (branchT[2], Output_2[26], Output_2[27], Output_2[26], nor_3_out);
  and and_5 (is_bltz, nor_1_out, nor_3_out, Output_2[26]);
  nor nor_3 (nor_3_out, Output_2[29], Output_2[30], Output_2[31]);
  or or_1 (branch, is_beq, is_bne, is_blez, branchT[2], is_bltz);
  or or_2 (branchT[1], is_bltz, is_blez);
  or or_3 (or_3_out, is_bne, is_blez);
  or or_4 (branchT[0], or_3_out, branchT[2]);
  nor nor_4 (nor_4_out, Output_2[29], Output_2[30], Output_2[31]);
  buf and_6 (and_6_out, nor_4_out);  // AND_Gate
  and and_7 (isJr, and_6_out, nRt_Rd);
  or or_5 (push_pop, is_push, is_pop);
  nor nor_5 (nor_5_out, Output[1], Output[2], Output[3], Output[4], Output[5]);
  and and_8 (is_push, Output[0], nor_5_out, nRt_Rd);
  and and_9 (is_pop, nor_6_out, _111000);
  nor nor_6 (nor_6_out, Output[0], Output[1], Output[2], Output[3], Output[4], Output[5]);
  and and_10 (is_sw, Output_2[26], Output_2[27], ~Output_2[28], Output_2[29], ~Output_2[30], Output_2[31]);  // AND_Gate
  and and_11 (is_lw, Output_2[26], Output_2[27], ~Output_2[28], ~Output_2[29], ~Output_2[30], Output_2[31]);  // AND_Gate
  and and_12 (isJ, Output_2[27], nor_7_out);
  nor nor_7 (nor_7_out, Output_2[26], Output_2[28], Output_2[29], Output_2[30], Output_2[31]);
  nor nor_8 (nor_8_out, Output_2[26], Output_2[27], Output_2[28], Output_2[29], Output_2[30], Output_2[31]);
  nor nor_9 (nor_9_out, Output_2[26], Output_2[27], Output_2[28]);
  and and_13 (and_13_out, Output_2[29], Output_2[30], Output_2[31]);
  and and_14 (and_14_out, Output_2[26], Output_2[27], Output_2[28], Output_2[29], Output_2[30], Output_2[31]);
  and and_15 (_111000, nor_9_out, and_13_out);
  nor nor_10 (nop, Output_2[27], Output_2[31], Output_2[30], Output_2[29], Output_2[28], Output_2[27], Output_2[26], Output_2[25], Output_2[24], Output_2[23], Output_2[22], Output_2[21], Output_2[20], Output_2[19], Output_2[18], Output_2[17], Output_2[15], Output_2[14], Output_2[13], Output_2[12], Output_2[11], Output_2[10], Output_2[9], Output_2[8], Output_2[7], Output_2[6], Output[5], Output[4], Output[3], Output[2], Output[1], Output[0]);
  or or_6 (nRt_Rd, nor_8_out, _111000, and_14_out);
  nor nor_11 (I, isJ, nRt_Rd);

  assign {Output_2[16], Output_2[5:0]} = {Output_2[27], Output};
  assign Output_3 = Output_2[15:11];
  assign Output_4 = {Output_2[20:17], Output_2[27]};
  assign Output_5 = {Output_2[25:17], Output_2[27], Output_2[15:6], Output};
  assign Output_6 = Output_2[25:21];
  assign Output_7 = {Output_2[15:6], Output};
  assign Output_8 = Output_2[31:26];

  // Other names for the same wires on the sheet: branchType[2:0] = branchT; is_bgtz = branchT[2];
  //   func_code[5:0] = Output; inst[31:0] = {Output_2[31:17], Output_2[27], Output_2[15:6], Output};
  //   jump[25:0] = {Output_2[25:17], Output_2[27], Output_2[15:6], Output}; offset[15:0] = {Output_2[15:6], Output};
  //   rd[4:0] = Output_2[15:11]; rt[4:0] = {Output_2[20:17], Output_2[27]}; rs[4:0] = Output_2[25:21];
  //   op_code[5:0] = Output_2[31:26]; J = isJ; jr = isJr; R = nRt_Rd

  // Notes on the sheet:
  //   BRANCHES
  //   JUMPS
  //   Output
  //   MEMORY
  //   Input
  //   INSTRUCTION TYPE
endmodule

module Data_Path (
  input  [5:0] func_code,
  input  [6:0] kbd,
  input  [31:0] in_3,
  input  [5:0] op_code,
  input  rst,
  input  in_6,
  input  clk,
  input  [15:0] offset,
  input  stackOp,
  input  [4:0] Rd,
  input  [31:0] Instruction,
  input  [4:0] Rt,
  input  in_13,
  input  [4:0] Rs,
  input  in_15
);

  wire undriven_2;
  wire [4:0] multiplexer_1_out, multiplexer_3_out, multiplexer_4_out, multiplexer_5_out;
  wire [31:0] bit_extender_1_out, Hi, Lo, multiplexer_2_out, undriven;

  assign bit_extender_1_out = {{25{kbd[6]}}, kbd};  // Bit_Extender bit_extender_1
  Multiplexer #(.width(5), .enable("false")) multiplexer_1 (.in0(Rt), .in1(Rd), .out(multiplexer_1_out), .sel(in_13));
  Multiplexer #(.select(3), .width(32)) multiplexer_2 (
    .in0(undriven), .in1(Hi), .in2(Lo), .in3({32{1'b1}}), .in4(bit_extender_1_out), .out(multiplexer_2_out),
    .en(undriven_2));  // open: in5, in6, in7, sel
  Multiplexer #(.width(5), .enable("false")) multiplexer_3 (.in0(Rt), .in1(Rs), .out(multiplexer_3_out), .sel(stackOp));
  Multiplexer #(.width(5), .enable("false")) multiplexer_4 (
    .in0(Rt), .in1({5{1'b1}}), .out(multiplexer_4_out), .sel(stackOp));
  Multiplexer #(.width(5), .enable("false")) multiplexer_5 (
    .in0(multiplexer_1_out), .in1({5{1'b1}}), .out(multiplexer_5_out), .sel(stackOp));
  Register_File register_file_1 (
    .Reset(rst), .DI(multiplexer_2_out), .Clk(clk), .DA(multiplexer_5_out), .A(multiplexer_3_out),
    .B(multiplexer_4_out), .HI_value_2(Hi), .LO_value_2(Lo));  // open: RW, RA, RB, Stack_Pointer, HI_value, LO_value, MD
  ALU alu_1 ();  // open: A, B, in_3, RESULT, HIGH, ZF, NF

  // Other names for the same wires on the sheet: inst[31:0] = Instruction; KBD_DATA[6:0] = kbd; nR_W = in_6;
  //   nRt_Rd = in_13; pc[31:0] = in_3; push_pop = stackOp; RW = in_15

  // Notes on the sheet:
  //   selector de DI
  //   Input
endmodule

module _16_32_Sign_Extender (
  input  [15:0] in_1,
  output [31:0] Output
);

  Multiplexer #(.width(16)) multiplexer_1 (
    .in0({16{1'b0}}), .in1({16{1'b1}}), .out(Output[31:16]), .sel(in_1[15]));  // open: en

  assign Output[15:0] = in_1;

  // Notes on the sheet:
  //   SIGN EXTENDER
endmodule
